# Fritzing sketch layout (saved by Fritzing 0.9.9b)
breadboards: 1

parts:
  TSM4044 = IC, DIP package, 18 pins [chip_label=4044]
  LED1 = LED - 3mm [color="Red (633nm)" current=0.030 package="3 mm [THT]"]
  LED2 = LED - 3mm [color="Green (555nm)" current=0.030 package="3 mm [THT]"]
  R1 = Resistor [tolerance=±5% power=0.25 resistance=220 package=THT]
  R2 = Resistor [tolerance=±5% power=0.25 resistance=220 package=THT]
  R3 = Resistor [tolerance=±5% power=0.25 resistance=3.3k package=THT]
  R4 = Resistor [tolerance=±5% power=0.25 resistance=2.2k package=THT]
  Teensy_3_2 = Teensy 3.1
  S1 = Momentary Switch [package=ksa_sealed_tac_switch]
  R5 = Resistor [tolerance=±5% power=0.25 resistance=10k package=THT]

nets:
  N1: TSM4044.pin1, Teensy_3_2.D12
  N2: TSM4044.pin2, Teensy_3_2.D11
  N3: TSM4044.pin3, Teensy_3_2.D10
  N4: TSM4044.pin4, Teensy_3_2.D9
  N5: TSM4044.pin5, Teensy_3_2.D8
  N6: TSM4044.pin6, Teensy_3_2.D7
  N7: TSM4044.pin7, R4.Pin_1
  N8: TSM4044.pin8, Teensy_3_2.D6
  N9: TSM4044.pin9, TSM4044.pin10, R1.Pin_1, R2.Pin_1, R3.Pin_1, Teensy_3_2.GND, R5.Pin_1
  N10: TSM4044.pin11, Teensy_3_2.A5/D19
  N11: TSM4044.pin12, Teensy_3_2.A4/D18
  N12: TSM4044.pin13, Teensy_3_2.A3/D17
  N13: TSM4044.pin14, Teensy_3_2.A2/D16
  N14: TSM4044.pin15, Teensy_3_2.A1/D15
  N15: TSM4044.pin16, Teensy_3_2.A0/D14
  N16: TSM4044.pin17, Teensy_3_2.D13
  N17: TSM4044.pin18, Teensy_3_2.Vin, S1.2
  N18: LED1.cathode, Teensy_3_2.D4
  N19: LED1.anode, R1.Pin_0
  N20: LED2.cathode, Teensy_3_2.D3
  N21: LED2.anode, R2.Pin_0
  N22: R3.Pin_0, R4.Pin_0, Teensy_3_2.D5
  N23: Teensy_3_2.D2, S1.4, R5.Pin_0

custom parts:
  Teensy 3.1: The Teensy is a complete USB-based microcontoller development system, in a very small footprint, capable of implementing many types of projects. All programming is done via the USB port. No special programmer is needed, only a standard micro-USB cable and a PC or Macintosh with a USB port. It has a USB keyboard/mouse/joystick emulation stack and can be programmed through Arduino IDE.
